# Fritzing sketch Creative Day 5 - Project 101 (saved by Fritzing 0.9.10b)
breadboards: 1

parts:
  Part1 = Arduino Uno (Inventr.io)
  R1 = Resistor [tolerance=±5% power=0.25 resistance=220 package=THT]
  S1 = DIP Switch 3 Position
  R2 = Resistor [tolerance=±5% power=0.25 resistance=220 package=THT]
  R3 = Resistor [tolerance=±5% power=0.25 resistance=220 package=THT]

nets:
  N1: Part1.D9_PWM, R1.Pin_1
  N2: Part1.D10_PWM/SS, R2.Pin_1
  N3: Part1.D11_PWM/MOSI, R3.Pin_1
  N4: Part1.GND, R1.Pin_0, R3.Pin_0
  N5: S1.1, S1.2, S1.3

custom parts:
  Arduino Uno (Inventr.io): The Arduino Uno is a microcontroller board based on the ATmega328 (datasheet). It has 14 digital input/output pins (of which 6 can be used as PWM outputs), 6 analog inputs, a 16 MHz ceramic resonator, a USB connection, a power jack, an ICSP header, and a reset button. It contains everything needed to support the microcontroller; simply connect it to a computer with a USB cable or power it with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
