# Fritzing sketch 102-Traffic-Light (saved by Fritzing 0.9.10b)
breadboards: 1

parts:
  Part1 = Arduino Uno (Inventr.io)
  R1 = Resistor [tolerance=±5% power=0.25 resistance=10k package=THT]
  S1 = DIP Switch 3 Position
  R2 = Resistor [tolerance=±5% power=0.25 resistance=10k package=THT]
  R3 = Resistor [tolerance=±5% power=0.25 resistance=10k package=THT]
  R4 = Resistor [tolerance=±5% power=0.25 resistance=220 package=THT]
  LED1 = LED - 5mm [color="Red (633nm)" current=0.030 package="5 mm [THT]"]
  LED2 = LED - 5mm [color="Yellow (585nm)" current=0.030 package="5 mm [THT]"]
  LED3 = LED - 5mm [color="Green (555nm)" current=0.030 package="5 mm [THT]"]
  LED4 = LED - 5mm [color="Red (633nm)" current=0.030 package="5 mm [THT]"]
  LED5 = LED - 5mm [color="Green (555nm)" current=0.030 package="5 mm [THT]"]
  R5 = Resistor [tolerance=±5% power=0.25 resistance=220 package=THT]
  R6 = Resistor [tolerance=±5% power=0.25 resistance=220 package=THT]
  R7 = Resistor [tolerance=±5% power=0.25 resistance=220 package=THT]
  R8 = Resistor [tolerance=±5% power=0.25 resistance=220 package=THT]

nets:
  N1: Part1.D8, R1.Pin_1
  N2: Part1.D9_PWM, R2.Pin_1
  N3: Part1.D10_PWM/SS, R3.Pin_1
  N4: Part1.D11_PWM/MOSI, LED3.anode
  N5: Part1.D12/MISO, LED2.anode
  N6: Part1.D13/SCK, LED1.anode
  N7: Part1.D6_PWM, LED5.anode
  N8: Part1.D7, LED4.anode
  N9: Part1.5V, S1.1, S1.2, S1.3
  N10: Part1.GND, R1.Pin_0, R3.Pin_0, R4.Pin_0, R5.Pin_0, R6.Pin_0, R7.Pin_0, R8.Pin_0
  N11: R4.Pin_1, LED3.cathode
  N12: LED1.cathode, R6.Pin_1
  N13: LED2.cathode, R5.Pin_1
  N14: LED4.cathode, R7.Pin_1
  N15: LED5.cathode, R8.Pin_1

custom parts:
  Arduino Uno (Inventr.io): The Arduino Uno is a microcontroller board based on the ATmega328 (datasheet). It has 14 digital input/output pins (of which 6 can be used as PWM outputs), 6 analog inputs, a 16 MHz ceramic resonator, a USB connection, a power jack, an ICSP header, and a reset button. It contains everything needed to support the microcontroller; simply connect it to a computer with a USB cable or power it with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
