# Fritzing sketch 105-LED-Scanner (saved by Fritzing 0.9.10b)
breadboards: 1

parts:
  S1 = DIP Switch 3 Position  # not connected
  LED2 = LED - 3mm [color="Blue (430nm)" current=0.030 package="3 mm [THT]"]
  LED3 = LED - 3mm [color="Green (555nm)" current=0.030 package="3 mm [THT]"]
  LED5 = LED - 3mm [color="Red (633nm)" current=0.030 package="3 mm [THT]"]
  LED7 = LED - 3mm [color="Green (555nm)" current=0.030 package="3 mm [THT]"]
  R1 = Resistor [tolerance=±5% power=0.25 resistance=220 package=THT]
  R2 = Resistor [tolerance=±5% power=0.25 resistance=220 package=THT]
  R3 = Resistor [tolerance=±5% power=0.25 resistance=220 package=THT]
  R4 = Resistor [tolerance=±5% power=0.25 resistance=220 package=THT]
  R5 = Resistor [tolerance=±5% power=0.25 resistance=220 package=THT]
  R6 = Resistor [tolerance=±5% power=0.25 resistance=220 package=THT]
  R7 = Resistor [tolerance=±5% power=0.25 resistance=220 package=THT]
  R8 = Resistor [tolerance=±5% power=0.25 resistance=10k package=THT]
  R9 = Resistor [tolerance=±5% power=0.25 resistance=10k package=THT]
  R10 = Resistor [tolerance=±5% power=0.25 resistance=10k package=THT]
  LED4 = LED - 3mm [color="Yellow (585nm)" current=0.030 package="3 mm [THT]"]
  LED8 = LED - 3mm [color="Yellow (585nm)" current=0.030 package="3 mm [THT]"]
  LED6 = LED - 3mm [color="Blue (430nm)" current=0.030 package="3 mm [THT]"]
  LED9 = LED - 3mm [color="Red (633nm)" current=0.030 package="3 mm [THT]"]
  R11 = Resistor [tolerance=±5% power=0.25 resistance=220 package=THT]
  Part1 = Arduino Uno (Inventr.io)

nets:
  N1: LED2.cathode, R3.Pin_0
  N2: LED2.anode, Part1.D12/MISO
  N3: LED3.cathode, R1.Pin_1
  N4: LED3.anode, Part1.D11_PWM/MOSI
  N5: LED5.cathode, R7.Pin_0
  N6: LED5.anode, Part1.D9_PWM
  N7: LED7.cathode, R5.Pin_0
  N8: LED7.anode, Part1.D7
  N9: R1.Pin_0, R2.Pin_1, R3.Pin_1, R4.Pin_1, R5.Pin_1, R6.Pin_1, R7.Pin_1, R8.Pin_1, R9.Pin_1, R10.Pin_1, R11.Pin_1, Part1.GND
  N10: R2.Pin_0, LED8.cathode
  N11: R4.Pin_0, LED4.cathode
  N12: R6.Pin_0, LED6.cathode
  N13: R8.Pin_0, Part1.D4
  N14: R9.Pin_0, Part1.D2
  N15: R10.Pin_0, Part1.D3_PWM
  N16: LED4.anode, Part1.D6_PWM
  N17: LED8.anode, Part1.D10_PWM/SS
  N18: LED6.anode, Part1.D8
  N19: LED9.cathode, R11.Pin_0
  N20: LED9.anode, Part1.D13/SCK

custom parts:
  Arduino Uno (Inventr.io): The Arduino Uno is a microcontroller board based on the ATmega328 (datasheet). It has 14 digital input/output pins (of which 6 can be used as PWM outputs), 6 analog inputs, a 16 MHz ceramic resonator, a USB connection, a power jack, an ICSP header, and a reset button. It contains everything needed to support the microcontroller; simply connect it to a computer with a USB cable or power it with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
