# Fritzing sketch 106-LED-Dice-v2 (saved by Fritzing 0.9.10b)
breadboards: 1

parts:
  S1 = DIP Switch 3 Position
  LED3 = LED - 3mm [color="Red (633nm)" current=0.030 package="3 mm [THT]"]
  R1 = Resistor [tolerance=±5% power=0.25 resistance=220 package=THT]
  R2 = Resistor [tolerance=±5% power=0.25 resistance=220 package=THT]
  R4 = Resistor [tolerance=±5% power=0.25 resistance=220 package=THT]
  R5 = Resistor [tolerance=±5% power=0.25 resistance=220 package=THT]
  R6 = Resistor [tolerance=±5% power=0.25 resistance=220 package=THT]
  R7 = Resistor [tolerance=±5% power=0.25 resistance=220 package=THT]
  R9 = Resistor [tolerance=±5% power=0.25 resistance=10k package=THT]
  Part1 = Arduino Uno (Inventr.io)
  LED8 = LED - 3mm [color="Red (633nm)" current=0.030 package="3 mm [THT]"]
  R10 = Resistor [tolerance=±5% power=0.25 resistance=220 package=THT]
  LED9 = LED - 3mm [color="Red (633nm)" current=0.030 package="3 mm [THT]"]  # not connected
  LED10 = LED - 3mm [color="Red (633nm)" current=0.030 package="3 mm [THT]"]
  LED11 = LED - 3mm [color="Red (633nm)" current=0.030 package="3 mm [THT]"]
  LED12 = LED - 3mm [color="Red (633nm)" current=0.030 package="3 mm [THT]"]
  LED13 = LED - 3mm [color="Red (633nm)" current=0.030 package="3 mm [THT]"]

nets:
  N1: S1.1, R9.Pin_0, Part1.D6_PWM
  N2: S1.6, Part1.5V
  N3: LED3.cathode, Part1.D12/MISO
  N4: LED3.anode, R1.Pin_1
  N5: R1.Pin_0, R2.Pin_1, R4.Pin_1, R5.Pin_1, R6.Pin_1, R7.Pin_1, R9.Pin_1, Part1.GND, R10.Pin_1
  N6: R2.Pin_0, LED11.anode
  N7: R4.Pin_0, LED12.anode
  N8: R6.Pin_0, LED8.anode
  N9: R7.Pin_0, LED10.anode
  N10: Part1.D8, LED13.cathode
  N11: Part1.D9_PWM, LED8.cathode
  N12: Part1.D10_PWM/SS, LED10.cathode
  N13: Part1.D13/SCK, LED11.cathode
  N14: Part1.D7, LED12.cathode
  N15: R10.Pin_0, LED13.anode

custom parts:
  Arduino Uno (Inventr.io): The Arduino Uno is a microcontroller board based on the ATmega328 (datasheet). It has 14 digital input/output pins (of which 6 can be used as PWM outputs), 6 analog inputs, a 16 MHz ceramic resonator, a USB connection, a power jack, an ICSP header, and a reset button. It contains everything needed to support the microcontroller; simply connect it to a computer with a USB cable or power it with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
