# Fritzing sketch 107-LED-Matrix (saved by Fritzing 0.9.10b)
breadboards: 1

parts:
  S1 = DIP Switch 3 Position
  LED3 = LED - 3mm [color="Red (633nm)" current=0.030 package="3 mm [THT]"]
  R9 = Resistor [tolerance=±5% power=0.25 resistance=10k package=THT]
  Part1 = Arduino Uno (Inventr.io)
  LED14 = LED - 3mm [color="Red (633nm)" current=0.030 package="3 mm [THT]"]
  LED15 = LED - 3mm [color="Red (633nm)" current=0.030 package="3 mm [THT]"]
  R13 = Resistor [tolerance=±5% power=0.25 resistance=10k package=THT]
  R14 = Resistor [tolerance=±5% power=0.25 resistance=10k package=THT]
  LED16 = LED - 3mm [color="Red (633nm)" current=0.030 package="3 mm [THT]"]
  R16 = Resistor [tolerance=±5% resistance=220 package="2010 [SMD]"]
  R17 = Resistor [tolerance=±5% resistance=220 package="2010 [SMD]"]
  R18 = Resistor [tolerance=±5% resistance=220 package="2010 [SMD]"]
  R19 = Resistor [tolerance=±5% resistance=220 package="2010 [SMD]"]
  R20 = Resistor [tolerance=±5% resistance=220 package="2010 [SMD]"]
  R21 = Resistor [tolerance=±5% resistance=220 package="2010 [SMD]"]
  R22 = Resistor [tolerance=±5% resistance=220 package="2010 [SMD]"]
  R23 = Resistor [tolerance=±5% resistance=220 package="2010 [SMD]"]
  R24 = Resistor [tolerance=±5% resistance=220 package="2010 [SMD]"]
  LED17 = LED - 3mm [color="Red (633nm)" current=0.030 package="3 mm [THT]"]
  LED18 = LED - 3mm [color="Red (633nm)" current=0.030 package="3 mm [THT]"]
  LED19 = LED - 3mm [color="Red (633nm)" current=0.030 package="3 mm [THT]"]
  LED20 = LED - 3mm [color="Red (633nm)" current=0.030 package="3 mm [THT]"]
  LED21 = LED - 3mm [color="Red (633nm)" current=0.030 package="3 mm [THT]"]

nets:
  N1: S1.1, Part1.A1, R13.Pin_0
  N2: S1.2, R9.Pin_0, Part1.A2
  N3: S1.3, Part1.A3, R14.Pin_0
  N4: S1.4, S1.5, S1.6, Part1.5V
  N5: LED3.cathode, Part1.D11_PWM/MOSI
  N6: LED3.anode, R16.Pin_1
  N7: R9.Pin_1, Part1.GND, R13.Pin_1, R14.Pin_1, R16.Pin_0, R17.Pin_0, R18.Pin_0, R19.Pin_0, R20.Pin_0, R21.Pin_0, R22.Pin_0, R23.Pin_0, R24.Pin_0
  N8: Part1.D8, LED16.cathode
  N9: Part1.D9_PWM, LED18.cathode
  N10: Part1.D10_PWM/SS, LED17.cathode
  N11: Part1.D12/MISO, LED15.cathode
  N12: Part1.D13/SCK, LED14.cathode
  N13: Part1.D5_PWM, LED19.cathode
  N14: Part1.D6_PWM, LED21.cathode
  N15: Part1.D7, LED20.cathode
  N16: LED14.anode, R18.Pin_1
  N17: LED15.anode, R17.Pin_1
  N18: LED16.anode, R19.Pin_1
  N19: R20.Pin_1, LED18.anode
  N20: R21.Pin_1, LED17.anode
  N21: R22.Pin_1, LED19.anode
  N22: R23.Pin_1, LED21.anode
  N23: R24.Pin_1, LED20.anode

custom parts:
  Arduino Uno (Inventr.io): The Arduino Uno is a microcontroller board based on the ATmega328 (datasheet). It has 14 digital input/output pins (of which 6 can be used as PWM outputs), 6 analog inputs, a 16 MHz ceramic resonator, a USB connection, a power jack, an ICSP header, and a reset button. It contains everything needed to support the microcontroller; simply connect it to a computer with a USB cable or power it with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
