# Fritzing sketch 108-Fade (saved by Fritzing 0.9.10b)
breadboards: 1

parts:
  Part1 = Arduino Uno (Inventr.io)
  R4 = Resistor [tolerance=±5% power=0.25 resistance=220 package=THT]
  LED1 = LED - 5mm [color="Red (633nm)" current=0.030 package="5 mm [THT]"]
  LED2 = LED - 5mm [color="Red (633nm)" current=0.030 package="5 mm [THT]"]
  LED3 = LED - 5mm [color="Blue (430nm)" current=0.030 package="5 mm [THT]"]
  LED4 = LED - 5mm [color="Blue (430nm)" current=0.030 package="5 mm [THT]"]
  LED5 = LED - 5mm [color="Green (555nm)" current=0.030 package="5 mm [THT]"]
  LED6 = LED - 5mm [color="Green (555nm)" current=0.030 package="5 mm [THT]"]
  R5 = Resistor [tolerance=±5% power=0.25 resistance=220 package=THT]
  R6 = Resistor [tolerance=±5% power=0.25 resistance=220 package=THT]
  R7 = Resistor [tolerance=±5% power=0.25 resistance=220 package=THT]
  R8 = Resistor [tolerance=±5% power=0.25 resistance=220 package=THT]
  R9 = Resistor [tolerance=±5% power=0.25 resistance=220 package=THT]

nets:
  N1: Part1.D9_PWM, LED4.anode
  N2: Part1.D10_PWM/SS, LED5.anode
  N3: Part1.D11_PWM/MOSI, LED6.anode
  N4: Part1.GND, R4.Pin_0, R5.Pin_0, R6.Pin_0, R7.Pin_0, R8.Pin_0, R9.Pin_0
  N5: Part1.D3_PWM, LED1.anode
  N6: Part1.D5_PWM, LED2.anode
  N7: Part1.D6_PWM, LED3.anode
  N8: R4.Pin_1, LED6.cathode
  N9: LED1.cathode, R9.Pin_1
  N10: LED2.cathode, R8.Pin_1
  N11: LED3.cathode, R7.Pin_1
  N12: LED4.cathode, R6.Pin_1
  N13: LED5.cathode, R5.Pin_1

custom parts:
  Arduino Uno (Inventr.io): The Arduino Uno is a microcontroller board based on the ATmega328 (datasheet). It has 14 digital input/output pins (of which 6 can be used as PWM outputs), 6 analog inputs, a 16 MHz ceramic resonator, a USB connection, a power jack, an ICSP header, and a reset button. It contains everything needed to support the microcontroller; simply connect it to a computer with a USB cable or power it with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
