# Fritzing sketch 201-Light-Sensor-With-LEDs (saved by Fritzing 0.9.10b)
breadboards: 1

parts:
  LED2 = LED - 3mm [color="Blue (430nm)" current=0.030 package="3 mm [THT]"]
  LED3 = LED - 3mm [color="Green (555nm)" current=0.030 package="3 mm [THT]"]
  LED5 = LED - 3mm [color="Red (633nm)" current=0.030 package="3 mm [THT]"]
  LED7 = LED - 3mm [color="Green (555nm)" current=0.030 package="3 mm [THT]"]
  LED4 = LED - 3mm [color="Yellow (585nm)" current=0.030 package="3 mm [THT]"]
  LED8 = LED - 3mm [color="Yellow (585nm)" current=0.030 package="3 mm [THT]"]
  LED6 = LED - 3mm [color="Blue (430nm)" current=0.030 package="3 mm [THT]"]
  LED9 = LED - 3mm [color="Red (633nm)" current=0.030 package="3 mm [THT]"]
  Part1 = Arduino Uno (Inventr.io)
  R11 = Resistor [tolerance=±5% power=0.25 resistance=220 package=THT]
  LED10 = LED - 3mm [color="White (8000K)" current=0.030 package="3 mm [THT]"]
  LED11 = LED - 3mm [color="White (8000K)" current=0.030 package="3 mm [THT]"]
  R12 = Resistor [tolerance=±5% power=0.25 resistance=220 package=THT]
  R13 = Resistor [tolerance=±5% power=0.25 resistance=220 package=THT]
  R14 = Resistor [tolerance=±5% power=0.25 resistance=220 package=THT]
  R15 = Resistor [tolerance=±5% power=0.25 resistance=220 package=THT]
  R16 = Resistor [tolerance=±5% power=0.25 resistance=220 package=THT]
  R17 = Resistor [tolerance=±5% power=0.25 resistance=220 package=THT]
  R18 = Resistor [tolerance=±5% power=0.25 resistance=220 package=THT]
  R19 = Resistor [tolerance=±5% power=0.25 resistance=220 package=THT]
  R20 = Resistor [tolerance=±5% power=0.25 resistance=220 package=THT]
  R21 = PHOTOCELL [package=photocell]
  R22 = Resistor [tolerance=±5% power=0.25 resistance=10k package=THT]

nets:
  N1: LED2.cathode, R11.Pin_1
  N2: LED2.anode, Part1.D11_PWM/MOSI
  N3: LED3.cathode, R18.Pin_1
  N4: LED3.anode, Part1.D4
  N5: LED5.cathode, R14.Pin_1
  N6: LED5.anode, Part1.D8
  N7: LED7.cathode, R17.Pin_1
  N8: LED7.anode, Part1.D5_PWM
  N9: LED4.cathode, R19.Pin_1
  N10: LED4.anode, Part1.D3_PWM
  N11: LED8.cathode, R20.Pin_1
  N12: LED8.anode, Part1.D2
  N13: LED6.cathode, R12.Pin_1
  N14: LED6.anode, Part1.D10_PWM/SS
  N15: LED9.cathode, R13.Pin_1
  N16: LED9.anode, Part1.D9_PWM
  N17: Part1.A0, R21.P$2, R22.Pin_1
  N18: Part1.GND, R11.Pin_0, R12.Pin_0, R13.Pin_0, R14.Pin_0, R15.Pin_0, R16.Pin_0, R17.Pin_0, R18.Pin_0, R19.Pin_0, R20.Pin_0, R22.Pin_0
  N19: Part1.D6_PWM, LED11.anode
  N20: Part1.D7, LED10.anode
  N21: Part1.5V, R21.P$1
  N22: LED10.cathode, R15.Pin_1
  N23: LED11.cathode, R16.Pin_1

custom parts:
  Arduino Uno (Inventr.io): The Arduino Uno is a microcontroller board based on the ATmega328 (datasheet). It has 14 digital input/output pins (of which 6 can be used as PWM outputs), 6 analog inputs, a 16 MHz ceramic resonator, a USB connection, a power jack, an ICSP header, and a reset button. It contains everything needed to support the microcontroller; simply connect it to a computer with a USB cable or power it with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
