# Fritzing sketch 202-Night-Light-With-LEDs (saved by Fritzing 0.9.10b)
breadboards: 1

parts:
  Part1 = Arduino Uno (Inventr.io)
  S1 = DIP Switch 3 Position
  R2 = Resistor [tolerance=±5% power=0.25 resistance=10k package=THT]
  R3 = Resistor [tolerance=±5% power=0.25 resistance=10k package=THT]
  R4 = Resistor [tolerance=±5% power=0.25 resistance=10k package=THT]
  LED2 = LED - 5mm [color="Blue (430nm)" current=0.030 package="5 mm [THT]"]
  R6 = Resistor [tolerance=±5% power=0.25 resistance=220 package=THT]
  LED5 = LED - 5mm [color="Red (660nm)" current=0.030 package="5 mm [THT]"]
  R8 = Resistor [tolerance=±5% power=0.25 resistance=220 package=THT]
  R9 = Resistor [tolerance=±5% power=0.25 resistance=220 package=THT]
  LED6 = LED - 5mm [color="Yellow (595nm)" current=0.030 package="5 mm [THT]"]
  R12 = Resistor [tolerance=±5% power=0.25 resistance=220 package=THT]
  R13 = PHOTOCELL [package=photocell]
  R14 = Resistor [tolerance=±5% power=0.25 resistance=10k package=THT]

nets:
  N1: Part1.A0, R13.P$1, R14.Pin_1
  N2: Part1.D9_PWM, LED2.anode
  N3: Part1.D10_PWM/SS, LED6.anode
  N4: Part1.D11_PWM/MOSI, LED5.anode
  N5: Part1.GND, R2.Pin_0, R3.Pin_0, R4.Pin_0, R6.Pin_0, R8.Pin_0, R9.Pin_0, R12.Pin_0, R14.Pin_0
  N6: Part1.D2, R4.Pin_1
  N7: Part1.D3_PWM, R3.Pin_1
  N8: Part1.D4, R2.Pin_1
  N9: Part1.5V, S1.1, S1.2, S1.3, R13.P$2
  N10: LED2.cathode, R8.Pin_1
  N11: R6.Pin_1, LED5.cathode
  N12: R9.Pin_1, LED6.cathode

custom parts:
  Arduino Uno (Inventr.io): The Arduino Uno is a microcontroller board based on the ATmega328 (datasheet). It has 14 digital input/output pins (of which 6 can be used as PWM outputs), 6 analog inputs, a 16 MHz ceramic resonator, a USB connection, a power jack, an ICSP header, and a reset button. It contains everything needed to support the microcontroller; simply connect it to a computer with a USB cable or power it with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
